// Logisim project lab4.circ as structural Verilog: 5 circuits, main circuit main
module main (
);

  wire alu_ctrl_1_alu_src, and_1_out, clock_1_out, comparator_1_eq, control_1_branch, control_1_memread,
       control_1_memtored, control_1_memwrite, control_1_regwrite;
  wire [3:0] alu_ctrl_1_alu_ctrl0;
  wire [7:0] register_1_q_2;
  wire [23:0] register_1_q;
  wire [31:0] adder_1_out, adder_2_out, alu32_1_r, datamemory_1_readdata, immgen_1_imm32,
       instructionmemory_1_instruction, multiplexer_1_out, multiplexer_2_out, register_file_1_p1,
       register_file_1_p7, register_file_1_p8;

  Register #(.width(32)) register_1 (
    .D(multiplexer_2_out), .en(1'b1), .clk(clock_1_out), .Q({register_1_q_2, register_1_q}));  // open: clr
  Clock clock_1 (.out(clock_1_out));
  Adder #(.width(32)) adder_1 (.a({register_1_q_2, register_1_q}), .b(32'h4), .out(adder_1_out));  // open: cin, cout
  InstructionMemory instructionmemory_1 (
    .Address(register_1_q), .Clock_in(clock_1_out), .Instruction(instructionmemory_1_instruction));
  Control control_1 (
    .I6_0(instructionmemory_1_instruction[6:0]), .MemtoRed(control_1_memtored),
    .RegWrite(control_1_regwrite), .MemRead(control_1_memread), .MemWrite(control_1_memwrite),
    .Branch(control_1_branch));
  // register_file register_file_1: pin names not known; wires that end beside it: register_file_1_p1, clock_1_out, control_1_regwrite, instructionmemory_1_instruction[11:7], instructionmemory_1_instruction[19:15], instructionmemory_1_instruction[24:20], register_file_1_p7, register_file_1_p8, register_file_1_p7
  IMMGen immgen_1 (.Instruction(instructionmemory_1_instruction), .IMM32(immgen_1_imm32));
  ALU_Ctrl alu_ctrl_1 (
    .i30(instructionmemory_1_instruction[31]), .i14(instructionmemory_1_instruction[14]),
    .i13(instructionmemory_1_instruction[13]), .i12(instructionmemory_1_instruction[12]),
    .i6(instructionmemory_1_instruction[6]), .i5(instructionmemory_1_instruction[5]),
    .i4(instructionmemory_1_instruction[4]), .ALU_CTRL3(alu_ctrl_1_alu_ctrl0[3]),
    .ALU_CTRL2(alu_ctrl_1_alu_ctrl0[2]), .ALU_CTRL1(alu_ctrl_1_alu_ctrl0[1]),
    .ALU_CTRL0(alu_ctrl_1_alu_ctrl0[0]), .ALU_SRC(alu_ctrl_1_alu_src));
  Multiplexer #(.enable("false"), .width(32)) multiplexer_1 (
    .in0(register_file_1_p8), .in1(immgen_1_imm32), .out(multiplexer_1_out), .sel(alu_ctrl_1_alu_src));
  Comparator #(.width(32)) comparator_1 (
    .a(register_file_1_p7), .b(register_file_1_p8), .eq(comparator_1_eq));  // open: gt, lt
  ALU32 alu32_1 (
    .ALU_Ctrl(alu_ctrl_1_alu_ctrl0), .A(register_file_1_p7), .B(multiplexer_1_out), .R(alu32_1_r));  // open: C_out
  Adder #(.width(32)) adder_2 (
    .a({register_1_q_2, register_1_q}), .b(immgen_1_imm32), .out(adder_2_out));  // open: cin, cout
  and and_1 (and_1_out, control_1_branch, comparator_1_eq);
  Multiplexer #(.enable("false"), .width(32)) multiplexer_2 (
    .in0(adder_1_out), .in1(adder_2_out), .out(multiplexer_2_out), .sel(and_1_out));
  DataMemory datamemory_1 (
    .Address(alu32_1_r[25:0]), .MemWrite(control_1_memwrite), .MemRead(control_1_memread),
    .Clock_in(clock_1_out), .WriteData(register_file_1_p8), .ReadData(datamemory_1_readdata));
  Multiplexer #(.enable("false"), .width(32)) multiplexer_3 (
    .in0(alu32_1_r), .in1(datamemory_1_readdata), .out(register_file_1_p1), .sel(control_1_memtored));
endmodule

module IMMGen (
  input  [31:0] Instruction,
  output [31:0] IMM32
);

  Multiplexer #(.enable("false"), .width(4)) multiplexer_1 (
    .in0(Instruction[24:21]), .in1(Instruction[11:8]), .out(IMM32[4:1]), .sel(Instruction[5]));
  Multiplexer #(.enable("false")) multiplexer_2 (
    .in0(Instruction[31]), .in1(Instruction[7]), .out(IMM32[11]), .sel(Instruction[6]));
  assign IMM32[31:12] = {{19{Instruction[31]}}, Instruction[31]};  // Bit_Extender bit_extender_1
  Multiplexer #(.enable("false"), .select(2)) multiplexer_3 (
    .in0(Instruction[20]), .in1(Instruction[7]), .in3(1'b0), .out(IMM32[0]), .sel(Instruction[6:5]));  // open: in2

  assign IMM32[10:5] = Instruction[30:25];

  // Other names for the same wires on the sheet: I30_25[5:0] = Instruction[30:25]; I5 = Instruction[5];
  //   I6_5[1:0] = Instruction[6:5]; I6 = Instruction[6]; I7 = Instruction[7]; I11_8[3:0] = Instruction[11:8];
  //   I20 = Instruction[20]; I24_21[3:0] = Instruction[24:21]; I31 = Instruction[31]
endmodule

module InstructionMemory (
  input  [23:0] Address,
  input  Clock_in,
  output [31:0] Instruction
);

  wire not_1_out;

  not not_1 (not_1_out, Clock_in);
  RAM #(.addrWidth(22), .asyncread("true"), .dataWidth(32)) ram_1 (
    .addr(Address[23:2]), .we(1'b0), .oe(not_1_out), .dout(Instruction));  // open: clk, din
endmodule

module DataMemory (
  input  [25:0] Address,
  input  MemWrite,
  input  MemRead,
  input  Clock_in,
  input  [31:0] WriteData,
  output [31:0] ReadData
);

  RAM #(.addrWidth(24), .asyncread("true"), .dataWidth(32)) ram_1 (
    .addr(Address[25:2]), .we(MemWrite), .oe(MemRead), .clk(Clock_in), .din(WriteData), .dout(ReadData));
endmodule

module Control (
  input  [6:0] I6_0,
  output MemtoRed,
  output RegWrite,
  output MemRead,
  output MemWrite,
  output Branch
);

  wire not_1_out, not_2_out;

  not not_1 (not_1_out, I6_0[6]);
  not not_2 (not_2_out, I6_0[5]);
  not not_3 (MemtoRed, I6_0[4]);
  or or_1 (RegWrite, not_2_out, I6_0[4]);
  and and_1 (MemRead, not_2_out, MemtoRed);
  and and_2 (MemWrite, not_1_out, I6_0[5], MemtoRed);

  assign Branch = I6_0[6];
endmodule
